// Digital circuit BW8cpu.dig as structural Verilog
module BW8cpu (
);

  wire a_dbus_a, a_dbus_l, a_lhs_a, a_rhs_a, addr_a, b_dbus_a, b_dbus_l, b_lhs_a, b_rhs_a, c_dbus_a,
       c_dbus_l, c_lhs_a, c_rhs_a, clk, clr, d_dbus_a, d_dbus_l, d_lhs_a, d_rhs_a, dbus_a, dbus_l, ir_dbus_l,
       lhs, mem_dbus_a, mem_dbus_l, rhs, xfer_a, xfer_l;
  wire [7:0] dbus, mbus;
  wire [15:0] addr_bus, xfer;

  control_unit Control_Unit ();  // open: mode, irq, clk, opcode, flags, dbus_assert, dbus_load, alu_op, xfer_assert, xfer_load, addr_assert, count, dec_sp, rst_useq, m_tog, brk_clk
  // instruction_register Instruction_Register: pin names not known; wires that end beside it: clk, dbus, ir_dbus_l, clr
  memory_bridge Memory_Bridge (.dbus_assert(mem_dbus_a), .dbus_load(mem_dbus_l), .dbus(dbus), .mbus(mbus));
  accumulator Accumulator (
    .a_dbus_load(a_dbus_l), .b_dbus_load(b_dbus_l), .a_dbus_assert(a_dbus_a), .b_dbus_assert(b_dbus_a),
    .a_lhs_assert(a_lhs_a), .b_lhs_assert(b_lhs_a), .a_rhs_assert(a_rhs_a), .b_rhs_assert(b_rhs_a),
    .dbus(dbus), .xfer(xfer), .clk(clk), .clr(clr), .addr(addr_bus));  // open: addr_assert, xfer_load, reg_a, reg_b
  direct_page_register DP_Register ();  // open: dbus, clk, clr, rhs, addr, assert_addr, assert_t1_dbus, assert_t1_rhs, assert_dp_dbus, load_t1_dbus, load_dp_dbus, reg_dp, reg_t1
  // general_purpose_register C_Register: pin names not known; wires that end beside it: clk, c_dbus_l, c_dbus_a, c_lhs_a, c_rhs_a, clr, dbus, lhs, rhs
  // general_purpose_register D_Register: pin names not known; wires that end beside it: clk, d_dbus_l, d_dbus_a, d_lhs_a, d_rhs_a, clr, dbus, lhs, rhs
  // bus_controller Bus_Controller: pin names not known; wires that end beside it: dbus_a, dbus_l, xfer_a, xfer_l, addr_a, a_dbus_a, b_dbus_a, c_dbus_a, d_dbus_a, mem_dbus_l, a_dbus_l, b_dbus_l, c_dbus_l, d_dbus_l, mem_dbus_a
  address_register Program_Counter ();  // open: xfer, clr, xfer_load, addr_assert, xfer_assert, inc, dec, clk, addr, reg
  address_register Stack_Pointer ();  // open: xfer, clr, xfer_load, addr_assert, xfer_assert, inc, dec, clk, addr, reg
  address_register X_Index ();  // open: xfer, clr, xfer_load, addr_assert, xfer_assert, inc, dec, clk, addr, reg
  address_register Y_Index ();  // open: xfer, clr, xfer_load, addr_assert, xfer_assert, inc, dec, clk, addr, reg
endmodule
